// Logisim project hack_architecture_CPU.circ as structural Verilog: 3 circuits, main circuit main
module main (
);

  _16_bits_Hack_ALU u_16_bits_hack_alu_1 ();  // open: x, y, Output_8bits, zr, ng, zx, zy, nx, ny, f, no
endmodule

module _16_bits_Hack_ALU (
  input  zx,
  input  zy,
  input  nx,
  input  ny,
  input  f,
  input  no,
  input  [15:0] x,
  input  [15:0] y,
  output [15:0] Output_8bits,
  output zr,
  output ng
);

  wire [15:0] adder_1_out, and_1_out, multiplexer_16_bits_1_out_4, multiplexer_16_bits_2_out_4,
       multiplexer_16_bits_3_out_4, multiplexer_16_bits_4_out_4, multiplexer_16_bits_5_out_4, not_1_out,
       not_2_out, not_3_out;

  Multiplexer_16_bits multiplexer_16_bits_1 (.A(x), .B({16{1'b0}}), .Select(zx), .out_4(multiplexer_16_bits_1_out_4));
  assign not_1_out = ~multiplexer_16_bits_1_out_4;  // NOT_Gate not_1, 16 bits wide
  Multiplexer_16_bits multiplexer_16_bits_2 (.A(y), .B({16{1'b0}}), .Select(zy), .out_4(multiplexer_16_bits_2_out_4));
  assign not_2_out = ~multiplexer_16_bits_2_out_4;  // NOT_Gate not_2, 16 bits wide
  Multiplexer_16_bits multiplexer_16_bits_3 (
    .A(multiplexer_16_bits_1_out_4), .B(not_1_out), .Select(nx), .out_4(multiplexer_16_bits_3_out_4));
  Multiplexer_16_bits multiplexer_16_bits_4 (
    .A(multiplexer_16_bits_2_out_4), .B(not_2_out), .Select(ny), .out_4(multiplexer_16_bits_4_out_4));
  assign and_1_out = multiplexer_16_bits_3_out_4 & multiplexer_16_bits_4_out_4;  // AND_Gate and_1, 16 bits wide
  Adder #(.width(16)) adder_1 (
    .a(multiplexer_16_bits_3_out_4), .b(multiplexer_16_bits_4_out_4), .out(adder_1_out), .cin(1'b0));  // open: cout
  Multiplexer_16_bits multiplexer_16_bits_5 (
    .A(and_1_out), .B(adder_1_out), .Select(f), .out_4(multiplexer_16_bits_5_out_4));
  assign not_3_out = ~multiplexer_16_bits_5_out_4;  // NOT_Gate not_3, 16 bits wide
  Multiplexer_16_bits multiplexer_16_bits_6 (
    .A(multiplexer_16_bits_5_out_4), .B(not_3_out), .Select(no), .out_4(Output_8bits));
  nand nand_1 (zr, Output_8bits[0], Output_8bits[1], Output_8bits[2], Output_8bits[3], Output_8bits[4], Output_8bits[5], Output_8bits[6], Output_8bits[7], Output_8bits[8], Output_8bits[9], Output_8bits[10], Output_8bits[11], Output_8bits[12], Output_8bits[13], Output_8bits[14], Output_8bits[15]);
  buf buffer_1 (ng, Output_8bits[15]);
endmodule

module Multiplexer_16_bits (
  input  [15:0] A,
  input  [15:0] B,
  input  Select,
  output [15:0] out_4
);

  wire [15:0] and_1_out, and_2_out, not_1_out;

  assign not_1_out = ~{16{Select}};  // NOT_Gate not_1, 16 bits wide
  assign and_1_out = A & not_1_out;  // AND_Gate and_1, 16 bits wide
  assign and_2_out = {16{Select}} & B;  // AND_Gate and_2, 16 bits wide
  assign out_4 = and_1_out | and_2_out;  // OR_Gate or_1, 16 bits wide

  // Other names for the same wires on the sheet: sel[15:0] = {16{Select}}
endmodule
